# Fritzing sketch Millefori (saved by Fritzing 1.0.3b)
perfboards: 1

parts:
  M2 = Niren can bus module [package=THT]  # not connected
  M3 = STM32F103C8T6 blue mini board
  A1 = 4-20ma to voltage converter
  A2 = 4-20ma to voltage converter  # not connected
  A3 = 4-20ma to voltage converter  # not connected
  A4 = 4-20ma to voltage converter  # not connected
  A5 = 4-20ma to voltage converter  # not connected
  A6 = 4-20ma to voltage converter  # not connected
  A7 = 4-20ma to voltage converter  # not connected
  A8 = 4-20ma to voltage converter  # not connected
  M4 = RioRand LM2596  # not connected
  M5 = RioRand LM2596  # not connected
  M6 = RioRand LM2596  # not connected
  J1 = Screw terminal - 2 pins [package=THT]
  C1 = Ceramic Capacitor [capacitance=100nF voltage=35V package="100 mil [THT, multilayer]"]
  C2 = Ceramic Capacitor [capacitance=100nF voltage=35V package="100 mil [THT, multilayer]"]
  C3 = Ceramic Capacitor [capacitance=100nF voltage=35V package="100 mil [THT, multilayer]"]
  C4 = Ceramic Capacitor [capacitance=100nF voltage=35V package="100 mil [THT, multilayer]"]
  C5 = Ceramic Capacitor [capacitance=100nF voltage=35V package="100 mil [THT, multilayer]"]
  C6 = Ceramic Capacitor [capacitance=100nF voltage=35V package="100 mil [THT, multilayer]"]
  C7 = Ceramic Capacitor [capacitance=100nF voltage=35V package="100 mil [THT, multilayer]"]
  VR1 = Trimpot-#3296-flat [package=3386u]
  VR2 = Trimpot-#3296-flat [package=3386u]
  VR3 = Trimpot-#3296-flat [package=3386u]
  VR4 = Trimpot-#3296-flat [package=3386u]
  VR5 = Trimpot-#3296-flat [package=3386u]
  VR6 = Trimpot-#3296-flat [package=3386u]
  VR7 = Trimpot-#3296-flat [package=3386u]
  VR8 = Trimpot-#3296-flat [package=3386u]
  J2 = Screw terminal - 2 pins [package=THT]
  J3 = Screw terminal - 2 pins [package=THT]
  J4 = Screw terminal - 2 pins [package=THT]
  J5 = Screw terminal - 2 pins [package=THT]
  J6 = Screw terminal - 2 pins [package=THT]
  J7 = Screw terminal - 2 pins [package=THT]
  J8 = Screw terminal - 2 pins [package=THT]
  C8 = Ceramic Capacitor [capacitance=100nF voltage=35V package="100 mil [THT, multilayer]"]
  D1 = Zener Diode [part_number=1N4732A breakdown_voltage=3.6V package="300 mil [THT]"]
  D2 = Zener Diode [part_number=1N4732A breakdown_voltage=3.6V package="300 mil [THT]"]
  D3 = Zener Diode [part_number=1N4732A breakdown_voltage=3.6V package="300 mil [THT]"]
  D4 = Zener Diode [part_number=1N4732A breakdown_voltage=3.6V package="300 mil [THT]"]
  D5 = Zener Diode [part_number=1N4732A breakdown_voltage=3.6V package="300 mil [THT]"]
  D6 = Zener Diode [part_number=1N4732A breakdown_voltage=3.6V package="300 mil [THT]"]
  D7 = Zener Diode [part_number=1N4732A breakdown_voltage=3.6V package="300 mil [THT]"]
  D8 = Zener Diode [part_number=1N4732A breakdown_voltage=3.6V package="300 mil [THT]"]

nets:
  N1: M3.A0, VR1.CCW
  N2: M3.A1, VR2.CCW
  N3: M3.A2, VR3.CCW
  N4: M3.A3, VR4.CCW
  N5: M3.A4, VR5.CCW
  N6: M3.A5, VR6.CCW
  N7: M3.A6, VR7.CCW
  N8: M3.A7, VR8.CCW
  GND: A1.Pin_3, J1.pin2, C1.0, C2.0, C3.0, C4.0, C5.0, C6.0, C7.0, J2.pin2, J3.pin2, J4.pin2, J5.pin2, J6.pin2, J7.pin2, J8.pin2, C8.0, D1.anode, D2.anode, D3.anode, D4.anode, D5.anode, D6.anode, D7.anode, D8.anode
  N9: J1.pin1, C1.1, VR1.WIPER
  N10: C2.1, VR2.WIPER, J4.pin1, D7.cathode
  N11: C3.1, VR3.WIPER, J2.pin1, D6.cathode
  N12: C4.1, VR4.WIPER, J3.pin1, D5.cathode
  N13: C5.1, VR5.WIPER, J5.pin1, D4.cathode
  N14: C6.1, VR6.WIPER, J6.pin1, D3.cathode
  N15: C7.1, VR7.WIPER, J7.pin1, D2.cathode
  N16: VR8.WIPER, J8.pin1, C8.1

custom parts:
  Niren can bus module: Niren can bus module availabe on ebay and others. Pcb view assumes that you unsolder the 7 pin header and resolder it on the bottom of the module to connect to the pcb. The two jumpers and the can bus connector remain on the top of the board and don't appear in pcb view.
  4-20ma to voltage converter: 4-20ma to voltage converter.
  Trimpot-#3296-flat: Bourns #3296 Square Trimpot 25 turn lying flat for low profile
